// Logisim project Oblig2.circ as structural Verilog: 7 circuits, main circuit main
module main (
  input  Clear
);

  wire and_1_out, Clock_out, Counter_check_out__1_on_done, Load, LSB, MSB, not_1_out, Write, xor_1_out,
       xor_2_out;
  wire [3:0] Counter_bits_ut, Counter_i_ut, ram_1_data_2;
  wire [7:0] changelsb_1_data_out, changemsb_1_data_out, multiplexer_1_out, multiplexer_2_out, R_q,
       ram_2_data;
  wire [7:4] ram_1_data;

  Clock Clock (.out(Clock_out));
  and and_1 (and_1_out, Clock_out, not_1_out);
  Counter Counter (
    .Bits_in(Counter_bits_ut), .Clock_Signal(and_1_out), .Clear(Clear), .I_ut(Counter_i_ut),
    .Bits_ut(Counter_bits_ut), .Check_out__1_on_done(Counter_check_out__1_on_done));
  not not_1 (not_1_out, Counter_check_out__1_on_done);
  RAM #(.addrWidth(4)) ram_1 (
    .addr(Counter_i_ut), .data({ram_1_data, ram_1_data_2}), .clk(Clock_out));  // open: sel, ld, clr
  Multiplexer #(.width(8)) multiplexer_1 (
    .in0(changemsb_1_data_out), .in1(changelsb_1_data_out), .out(multiplexer_1_out), .sel(LSB), .en(Clock_out));
  ChangeMSB changemsb_1 (.Old_Data(R_q), .New_Data({ram_1_data, ram_1_data_2}), .Data_Out(changemsb_1_data_out));
  // NAND_Gate nand_1 is placed but not wired
  ChangeLSB changelsb_1 (.New_Data({ram_1_data, ram_1_data_2}), .Old_Data(R_q), .Data_Out(changelsb_1_data_out));
  Controller Controller (
    .Instruksjon_inn({ram_1_data, ram_1_data_2}), .LSB(LSB), .MSB(MSB), .Load(Load), .Write(Write));
  Multiplexer #(.width(8)) multiplexer_2 (
    .in0(multiplexer_1_out), .in1(ram_2_data), .out(multiplexer_2_out), .sel(Load), .en(Clock_out));
  Register #(.trigger("falling")) R (.D(multiplexer_2_out), .en(xor_1_out), .Q(R_q), .clk(Clock_out), .clr(Clear));
  xor xor_1 (xor_1_out, xor_2_out, Load);
  xor xor_2 (xor_2_out, LSB, MSB);
  RAM #(.addrWidth(4), .bus("separate")) ram_2 (
    .addr(ram_1_data_2), .din(R_q), .data(ram_2_data), .str(Write), .clk(Clock_out), .clr(Clear));  // open: sel, ld
  // OR_Gate or_1 is placed but not wired

  // Notes on the sheet:
  //   Instruksjoner
  //   (s7...s0)
  //   RAM
endmodule

// HA
module HalvAdder (
  input  Bit_inn,
  input  Bit_inn_2,
  output Carry_ut,
  output Bit_ut
);

  and and_1 (Carry_ut, Bit_inn, Bit_inn_2);
  xor xor_1 (Bit_ut, Bit_inn, Bit_inn_2);
endmodule

// FA
module FullAdder (
  input  Bit_inn,
  input  Bit_inn_2,
  input  Carry_inn,
  output Carry_ut,
  output Bit_ut
);

  wire and_1_out, and_2_out, xor_1_out;

  and and_1 (and_1_out, Bit_inn, Bit_inn_2);
  xor xor_1 (xor_1_out, Bit_inn, Bit_inn_2);
  and and_2 (and_2_out, xor_1_out, Carry_inn);
  xor xor_2 (Bit_ut, xor_1_out, Carry_inn);
  xor xor_3 (Carry_ut, and_1_out, and_2_out);
endmodule

module Counter (
  input  [3:0] Bits_in,
  input  Clock_Signal,
  input  Clear,
  output [3:0] I_ut,
  output [3:0] Bits_ut,
  output Check_out__1_on_done
);

  wire fulladder_1_carry_ut, fulladder_2_carry_ut, fulladder_3_carry_ut, halvadder_1_carry_ut;

  Register #(.width(4), .trigger("falling")) Teller (
    .D(Bits_ut), .Q(I_ut), .clk(Clock_Signal), .clr(Clear));  // open: en
  FullAdder fulladder_1 (
    .Bit_inn(1'b0), .Bit_inn_2(I_ut[3]), .Carry_inn(fulladder_2_carry_ut), .Carry_ut(fulladder_1_carry_ut),
    .Bit_ut(Bits_ut[3]));
  FullAdder fulladder_2 (
    .Bit_inn(1'b0), .Bit_inn_2(I_ut[2]), .Carry_inn(fulladder_3_carry_ut), .Carry_ut(fulladder_2_carry_ut),
    .Bit_ut(Bits_ut[2]));
  FullAdder fulladder_3 (
    .Bit_inn(1'b0), .Bit_inn_2(I_ut[1]), .Carry_inn(halvadder_1_carry_ut), .Carry_ut(fulladder_3_carry_ut),
    .Bit_ut(Bits_ut[1]));
  Register #(.width(1), .trigger("falling")) Check_Reg (
    .D(fulladder_1_carry_ut), .Q(Check_out__1_on_done), .clk(Clock_Signal), .clr(Clear));  // open: en
  HalvAdder halvadder_1 (
    .Bit_inn(Clock_Signal), .Bit_inn_2(I_ut[0]), .Carry_ut(halvadder_1_carry_ut), .Bit_ut(Bits_ut[0]));
endmodule

module Controller (
  input  [7:0] Instruksjon_inn,
  output LSB,
  output MSB,
  output Load,
  output Write
);

  wire and_1_out, and_2_out, and_3_out, and_4_out, and_5_out, and_6_out, and_7_out, and_8_out, xor_1_out,
       xor_2_out, xor_3_out, xor_4_out, xor_5_out, xor_6_out, xor_7_out, xor_8_out, xor_9_out, xor_10_out,
       xor_11_out, xor_12_out;

  xor xor_1 (xor_1_out, Instruksjon_inn[5], Instruksjon_inn[6]);
  and and_1 (and_1_out, Instruksjon_inn[5], Instruksjon_inn[6]);
  xor xor_2 (xor_2_out, Instruksjon_inn[5], Instruksjon_inn[6]);
  and and_2 (and_2_out, Instruksjon_inn[5], Instruksjon_inn[6]);
  and and_3 (and_3_out, Instruksjon_inn[7], Instruksjon_inn[4]);
  xor xor_3 (xor_3_out, Instruksjon_inn[6], Instruksjon_inn[4]);
  and and_4 (and_4_out, Instruksjon_inn[6], Instruksjon_inn[4]);
  and and_5 (and_5_out, Instruksjon_inn[7], Instruksjon_inn[5]);
  and and_6 (and_6_out, Instruksjon_inn[4], Instruksjon_inn[5]);
  xor xor_4 (xor_4_out, xor_1_out, and_1_out);
  xor xor_5 (xor_5_out, xor_2_out, and_2_out);
  xor xor_6 (xor_6_out, xor_3_out, and_4_out);
  and and_7 (and_7_out, and_6_out, Instruksjon_inn[7]);
  xor xor_7 (xor_7_out, Instruksjon_inn[4], xor_4_out);
  and and_8 (and_8_out, Instruksjon_inn[4], xor_4_out);
  xor xor_8 (xor_8_out, xor_5_out, and_3_out);
  xor xor_9 (xor_9_out, xor_6_out, and_5_out);
  xor xor_10 (xor_10_out, and_7_out, Instruksjon_inn[6]);
  xor xor_11 (xor_11_out, xor_7_out, and_8_out);
  and and_9 (MSB, xor_8_out, and_3_out);
  and and_10 (Load, xor_9_out, and_5_out);
  and and_11 (Write, and_7_out, xor_10_out);
  xor xor_12 (xor_12_out, Instruksjon_inn[7], xor_11_out);
  and and_12 (LSB, Instruksjon_inn[7], xor_12_out);
endmodule

// LSB
module ChangeLSB (
  input  [7:0] New_Data,
  input  [7:0] Old_Data,
  output [7:0] Data_Out
);


  assign Data_Out = {Old_Data[7:4], New_Data[3:0]};
endmodule

// MSB
module ChangeMSB (
  input  [7:0] Old_Data,
  input  [7:0] New_Data,
  output [7:0] Data_Out
);


  assign Data_Out = {New_Data[3:0], Old_Data[3:0]};
endmodule
